# Fritzing sketch mux-schematic (saved by Fritzing 0.9.1b)
breadboards: 1

parts:
  IC1 = IC, DIP package, 16 pins [chip_label=CD4051B]

nets:
  ADC 10: IC1.pin1
  ADC 12: IC1.pin2
  BBB P9_35: IC1.pin3
  ADC 13: IC1.pin4
  ADC 11: IC1.pin5
  GND: IC1.pin6, IC1.pin7, IC1.pin8
  BBB P9_27: IC1.pin9
  BBB P9_30: IC1.pin10
  BBB P9_42: IC1.pin11
  ADC 9: IC1.pin12
  ADC 6: IC1.pin13
  ADC 7: IC1.pin14
  ADC 8: IC1.pin15
  3.3V: IC1.pin16
